# Fritzing sketch Circuit Diagram fritzing (saved by Fritzing 0.9.3b)

parts:
  U1 = ESP8266 NodeMCU LoLin module
  Part1 = RFID-RC522-v2
  SG1 = Buzzer 12mm [package=buzzer-ccv]
  LCD2004-I2C1 = LCD2004-I2C
  U2 = ESP8266 NodeMCU LoLin module
  Keypad4x1 = Keypad Membran 4x4

nets:
  N1: U1.D0, SG1.2
  N2: U1.D1, LCD2004-I2C1.SCL
  N3: U1.D2, LCD2004-I2C1.SDA
  N4: U1.D3, Part1.RST
  N5: U1.D4, Part1.SDA
  3V3: U1.3V3, Part1.3.3V, LCD2004-I2C1.VCC
  N6: U1.D5, Part1.SCK
  N7: U1.D6, Part1.MISO
  N8: U1.D7, Part1.MOSI
  GND: U1.GND, Part1.GND, SG1.1, LCD2004-I2C1.GND
  N9: U2.D0, Keypad4x1.Pin8
  N10: U2.D1, Keypad4x1.Pin7
  N11: U2.D2, Keypad4x1.Pin6
  N12: U2.D3, Keypad4x1.Pin5
  N13: U2.D4, Keypad4x1.Pin4
  N14: U2.D5, Keypad4x1.Pin3
  N15: U2.D6, Keypad4x1.Pin2
  N16: U2.D7, Keypad4x1.Pin1

custom parts:
  ESP8266 NodeMCU LoLin module: ESP8266 based NodeMCU
  RFID-RC522-v2: A simple China made RFID-RC522 Reader; do check the pin labels, as this is a MFRC522 based clone.
  LCD2004-I2C: A standard character display with 4x20 characters. Comes in many colors with LCM2004 IIC attached.
  Keypad Membran 4x4: Membrane Keypad 4x4 Matrix
